# Fritzing sketch prototype (saved by Fritzing 0.9.3b)
breadboards: 1

parts:
  Part1 = Arduino Uno (Rev3) - ICSP
  Pitch_Servo = Basic Servo
  Yaw_Servo = Basic Servo
  Laser_(not_LED) = LED - 5mm [color="Red (633nm)" package="5 mm [THT]"]

nets:
  GND: Part1.GND, Pitch_Servo.gnd, Yaw_Servo.gnd, Laser_(not_LED).cathode
  N1: Part1.D2, Yaw_Servo.pulse
  N2: Part1.D4, Pitch_Servo.pulse
  VCC: Part1.5V, Pitch_Servo.vcc, Yaw_Servo.vcc, Laser_(not_LED).anode
